# Fritzing sketch Hot_Wheels_Speed_Meter (saved by Fritzing 0.9.3b)
breadboards: 1

parts:
  Componente1 = Arduino Uno (Rev3)
  Mod1 = KY-032 IR Obstacle Avoidance Sensor Module [package="Breakout board"]
  U3 = LCD-16X2 [package=lcd-16x2_noholes]
  Mod3 = KY-032 IR Obstacle Avoidance Sensor Module [package="Breakout board"]
  R1 = Rotary Potentiometer (Large) [maximum_resistance=100kΩ package=THT]

nets:
  N1: Componente1.D8, Mod3.out
  N2: Componente1.D9_PWM, Mod1.out
  N3: Componente1.D11_PWM/MOSI, U3.E
  N4: Componente1.D12/MISO, U3.RS
  N5: Componente1.D2, U3.DB7
  N6: Componente1.D3_PWM, U3.DB6
  N7: Componente1.D4, U3.DB5
  N8: Componente1.D5_PWM, U3.DB4
  5V: Componente1.5V, Mod1.+, U3.VDD, U3.A, Mod3.+, R1.leg2
  GND: Componente1.GND, Mod1.GND, U3.VSS, U3.R_W, U3.K, Mod3.GND, R1.leg1
  N9: U3.VO, R1.wiper

notes:
  Sensor 1
  Sensor 2

custom parts:
  KY-032 IR Obstacle Avoidance Sensor Module: KY-032 Infrared Obstacle Avoidance Sensor. Distance-adjustable, infrared proximity sensor designed for wheeled robots. Also known as AD-032.
